# Fritzing sketch PCB-Scheme (saved by Fritzing 0.9.6b)
circuit board: 8cm x 6.5cm
circuit board: 8cm x 6.5cm
circuit board: 3.5cm x 5.5cm
breadboards: 1

parts:
  Arduino_Micro = Arduino Micro (Rev3)
  MCU1 = Raspberry Pi Zero
  J2 = Screw terminal - 2 pins [package=THT]
  LLC1 = Logic Level Converter [package="Breakout board"]
  Q1 = Basic FET P-Channel [package="TO220 [THT]"]
  PING = smd LED [color="Red (633nm)" package="0603 [SMD]"]
  R1 = Resistor [tolerance=±5% resistance=220 package="0805 [SMD]"]
  R2 = Resistor [tolerance=±5% resistance=220 package="0805 [SMD]"]  # not connected
  Switch = SPST Switch [package=switch-spst-smd-a]
  PowerUnit = RioRand LM2596
  MPU6050 = InvenSense MPU6050
  J3 = Screw terminal - 2 pins [package=THT]
  JP1 = Header 1 [package=1x01_offset]
  JP2 = Header 1 [package=1x01_offset]
  J8 = female pin header, 6 pins [form="♀ (female)"]
  J4 = female pin header, 2 pins [form="♀ (female)"]
  J9 = Screw terminal - 2 pins [package=THT]
  J10 = female pin header, 2 pins [form="♀ (female)"]  # not connected
  Sonar = female pin header, 4 pins [form="♀ (female)"]
  Arduino_Micro1 = Arduino Micro (Rev3)
  LLC2 = Logic Level Converter [package="Breakout board"]
  MCU2 = Raspberry Pi Zero
  J12 = Screw terminal - 2 pins [package=THT]
  J13 = female pin header, 6 pins [form="♀ (female)"]
  MPU6051 = InvenSense MPU6050
  Sonar1 = female pin header, 4 pins [form="♀ (female)"]

nets:
  N1: Arduino_Micro.D1/TX, J4.pin1
  N2: Arduino_Micro.D0/RX, J4.pin2
  GND: Arduino_Micro.GND, Q1.source, PING.cathode, PowerUnit.Pin_4, MPU6050.GND, J9.pin2
  N3: Arduino_Micro.D2/SDA, MPU6050.SDA
  N4: Arduino_Micro.D3/SCL, MPU6050.SCL
  N5: Arduino_Micro.D4_PWM/A6, J8.pin1
  N6: Arduino_Micro.D5_PWM, J8.pin2
  N7: Arduino_Micro.D6_PWM/A7, J8.pin3
  N8: Arduino_Micro.D7, J8.pin4
  N9: Arduino_Micro.D8_PWM/A8, J8.pin5
  N10: Arduino_Micro.D12_PWM/A11, J8.pin6
  VIN: Arduino_Micro.VIN, Q1.drain, PowerUnit.Pin_3, MPU6050.VCC, J9.pin1
  N11: Arduino_Micro.A2, PING.anode, R1.Pin_0, R1.Pin_1
  N12: Arduino_Micro.A1, Sonar.pin1
  N13: Arduino_Micro.A0, Sonar.pin2
  N14: MCU1.pin_2, MCU1.pin_4, LLC1.LV, LLC1.HV, J3.pin1
  N15: MCU1.pin_6, MCU1.pin_9, MCU1.pin_30, LLC1.L-GND, LLC1.H-GND, J3.pin2
  N16: MCU1.pin_8, LLC1.LV3
  N17: MCU1.pin_10, LLC1.LV4
  N18: J2.pin1, PowerUnit.Pin_2
  N19: J2.pin2, Switch.S
  N20: LLC1.HV4, JP1.1
  N21: LLC1.HV3, JP2.1
  N22: Switch.O, PowerUnit.Pin_1
  N23: Arduino_Micro1.D1/TX, LLC2.HV3
  N24: Arduino_Micro1.D0/RX, LLC2.HV4
  N25: Arduino_Micro1.D2/SDA, MPU6051.SDA
  N26: Arduino_Micro1.D3/SCL, MPU6051.SCL
  N27: Arduino_Micro1.D4_PWM/A6, J13.pin6
  N28: Arduino_Micro1.D5_PWM, J13.pin5
  N29: Arduino_Micro1.D6_PWM/A7, J13.pin4
  N30: Arduino_Micro1.D7, J13.pin3
  N31: Arduino_Micro1.D8_PWM/A8, J13.pin2
  N32: Arduino_Micro1.D12_PWM/A11, J13.pin1
  N33: Arduino_Micro1.A1, Sonar1.pin1
  N34: Arduino_Micro1.A0, Sonar1.pin2
  N35: LLC2.LV, MCU2.pin_1, MCU2.pin_17
  N36: LLC2.L-GND, LLC2.H-GND, MCU2.pin_6, MCU2.pin_14, MCU2.pin_25, MCU2.pin_34, J12.pin2, MPU6051.GND, Sonar1.pin4
  N37: LLC2.LV3, MCU2.pin_10
  N38: LLC2.HV, MCU2.pin_2, MCU2.pin_4, J12.pin1, MPU6051.VCC, Sonar1.pin3

custom parts:
  Logic Level Converter: 5V to/from 3.3V logic level converter
