# Fritzing sketch scheme (saved by Fritzing 0.9.3b)
circuit board: 15.4267cm x 7.35182cm
breadboards: 1

parts:
  Lm2596 = RioRand LM2596
  Arduino = Arduino Micro (Rev3)
  CameraX = Dagu DGServo 9g header connector (female) [package=THT]
  CameraY = Dagu DGServo 9g header connector (female) [package=THT]
  Buzzer = Microphone
  Ultrasonic = HY-SRF05 Ultrasonic Rangefinder
  S1 = Toggle Switch [package=THT]
  Power = Power plug
  ch1 = Header 4 [package=1x04-1mm-ra]
  ch2 = Header 4 [package=1x04-1mm-ra]

nets:
  GND: Lm2596.Pin_0, Arduino.GND, CameraX.pulse, CameraY.pulse, Buzzer.pin2, Ultrasonic.GND
  N1: Lm2596.Pin_1, Power.GND
  VCC: Lm2596.Pin_2, Arduino.5V, CameraX.Vcc, CameraY.Vcc
  N2: Lm2596.Pin_3, S1.L1
  N3: Arduino.D2/SDA, Buzzer.pin1
  N4: Arduino.D3/SCL, ch2.2
  N5: Arduino.D4_PWM/A6, ch2.3
  N6: Arduino.D5_PWM, ch2.4
  N7: Arduino.D6_PWM/A7, ch1.2
  N8: Arduino.D7, ch1.3
  N9: Arduino.D8_PWM/A8, ch1.4
  N10: Arduino.D10_PWM/A10, CameraX.gnd
  N11: Arduino.D11_PWM, Ultrasonic.Echo
  N12: Arduino.D12_PWM/A11, Ultrasonic.Vcc
  N13: S1.L2, Power.VCC
  N14: ch1.1, ch2.1
